# Fritzing sketch espixel (saved by Fritzing 0.9.2b)
breadboards: 1

parts:
  ESP8266-1 = ESP8266-12 [part_number=ESP8266-12]
  NEOPIXEL1 = Neopixel Strip -- White (30/m)
  VCC1 = Battery

nets:
  VCC: ESP8266-1.VCC, NEOPIXEL1.+5V, VCC1.+
  N1: ESP8266-1.GPIO2, NEOPIXEL1.Din
  GND: ESP8266-1.GND, NEOPIXEL1.GND, VCC1.-

custom parts:
  Neopixel Strip -- White (30/m): These NeoPixel strips have 30 digitally-addressable pixel LEDs per meter and are very affordable and are only 12.5 mm wide, 10 mm if you remove the strip from the casing.
